// Digital circuit TOP.dig as structural Verilog
module TOP (
  input  clk,
  input  [11:0] MIPCBI,
  input  MIPCBE,
  input  [15:0] PCBIA1,
  input  PCBE1,
  input  [15:0] PCBIA2,
  input  PCBE2
);

  wire and_1_out, and_2_out, and_3_out, button_2_out, button_3_out, button_4_out, CLK_t, CLR,
       comparator_1_eq, comparator_2_eq, comparator_3_eq, dipswitch_1_out, IRQ_CAI, IRQ_OE, nXRAM_OE,
       nXRAM_WE, or_1_out, RI, SFR_OE, SFR_WE, TI;
  wire [7:0] ADDR_SFR, ADDR_XRAM, BUS_D, INT_irq;
  wire [11:0] MIPC;
  wire [15:0] PC;

  Button button_1 (.out(CLR));
  RAMSinglePortSel #(.AddrBits(16), .isProgramMemory("true"), .Bits(8)) XRAM (
    .A({ADDR_SFR, ADDR_XRAM}), .CS(~1'b0), .WE(~nXRAM_WE), .OE(~nXRAM_OE), .D(BUS_D));
  Comparator #(.Bits(12)) comparator_1 (.a(MIPCBI), .b(MIPC), .eq(comparator_1_eq));  // open: gt, lt
  Comparator #(.Bits(16)) comparator_2 (.a(PCBIA1), .b(PC), .eq(comparator_2_eq));  // open: gt, lt
  Comparator #(.Bits(16)) comparator_3 (.a(PCBIA2), .b(PC), .eq(comparator_3_eq));  // open: gt, lt
  and and_1 (and_1_out, comparator_1_eq, MIPCBE);
  and and_2 (and_2_out, comparator_2_eq, PCBE1);
  and and_3 (and_3_out, comparator_3_eq, PCBE2);
  DipSwitch dipswitch_1 (.out(dipswitch_1_out));
  Button button_2 (.out(button_2_out));
  Button button_3 (.out(button_3_out));
  Button button_4 (.out(button_4_out));
  or or_1 (or_1_out, and_1_out, and_2_out, and_3_out);
  CORE core_1 (
    .GC(clk), .MC(button_2_out), .SWC(dipswitch_1_out), .GO(button_3_out), .RST(button_4_out), .CLR(CLR),
    .STALL(or_1_out), .PC(PC), .MIPC(MIPC), .IO(BUS_D), .ADDR({ADDR_SFR, ADDR_XRAM}), .nXRAM_WE(nXRAM_WE),
    .nXRAM_OE(nXRAM_OE), .CLK(SFR_WE), .nIRQ_OE(SFR_OE), .IRQ_CAI(CLK_t), .nSFR_WE(IRQ_OE), .nSFR_OE(IRQ_CAI));
  // Probe on PC
  // Probe on MIPC
  SBUF SBUF (.IO(BUS_D), .CLK(CLK_t), .A(ADDR_SFR), .OE(SFR_OE), .WE(SFR_WE), .RI(RI), .TI(TI));
  // EXTCTL EXT: pin names not known; wires that end beside it: SFR_WE, ADDR_SFR, BUS_D, CLK_t
  INT INT (
    .CLK(CLK_t), .CLR(CLR), .A(ADDR_SFR), .D(BUS_D), .WE(SFR_WE), .OE(SFR_OE), .nIRQ_OE(IRQ_OE),
    .CAI(IRQ_CAI), .RI(RI), .TI(TI), .IRQ(INT_irq));
  // DUMP DUMP: pin names not known; wires that end beside it: SFR_WE, ADDR_SFR, BUS_D, CLK_t
  // Probe on INT_irq

  // Other names for the same wires on the sheet: ADDR_XRAM[15:8] = ADDR_SFR

  // Notes on the sheet:
  //   clk: Hz: 2147483647
endmodule
